// Logisim project Octa e Mult.circ as structural Verilog
module Octa_bi (
  input  _0,
  input  _1,
  input  _2,
  input  _3,
  input  _4,
  input  _5,
  input  _6,
  input  _7,
  output [2:0] out_9
);

  or or_1 (out_9[2], _4, _5, _6, _7);
  or or_2 (out_9[1], _2, _3, _6, _7);
  or or_3 (out_9[0], _1, _3, _5, _7);
endmodule

module Conversor_Octa_7 (
  input  S1,
  input  S2,
  input  S3,
  output a,
  output b,
  output c,
  output d,
  output e,
  output f,
  output g
);

  wire and_1_out, and_2_out, and_3_out, and_4_out, and_5_out, and_6_out, and_7_out, and_8_out, and_9_out,
       and_10_out, and_11_out, and_12_out, and_13_out, and_14_out, and_15_out, and_16_out, not_1_out,
       not_2_out, not_3_out, not_4_out, not_5_out, not_6_out, not_7_out, not_8_out, not_9_out, not_10_out,
       not_11_out, not_12_out, not_13_out, not_14_out, not_15_out, not_16_out, not_17_out, not_18_out,
       not_19_out, not_20_out, not_21_out;

  not not_1 (not_1_out, S1);
  not not_2 (not_2_out, S3);
  not not_3 (not_3_out, S2);
  not not_4 (not_4_out, S3);
  not not_5 (not_5_out, S2);
  not not_6 (not_6_out, S1);
  not not_7 (not_7_out, S3);
  not not_8 (not_8_out, S1);
  not not_9 (not_9_out, S3);
  not not_10 (not_10_out, S2);
  not not_11 (not_11_out, S1);
  not not_12 (not_12_out, S3);
  not not_13 (not_13_out, S3);
  not not_14 (not_14_out, S2);
  not not_15 (not_15_out, S3);
  not not_16 (not_16_out, S2);
  not not_17 (not_17_out, S3);
  not not_18 (not_18_out, S1);
  not not_19 (not_19_out, S2);
  not not_20 (not_20_out, S3);
  and and_1 (and_1_out, not_1_out, not_2_out);
  and and_2 (and_2_out, S1, S3);
  not not_21 (not_21_out, S1);
  and and_3 (and_3_out, not_3_out, not_4_out);
  and and_4 (and_4_out, S2, S3);
  or or_1 (c, not_5_out, S3, S1);
  and and_5 (and_5_out, not_6_out, not_7_out);
  and and_6 (and_6_out, not_8_out, S2);
  and and_7 (and_7_out, S2, not_9_out);
  and and_8 (and_8_out, S1, not_10_out, S3);
  and and_9 (and_9_out, not_11_out, not_12_out);
  and and_10 (and_10_out, S2, not_13_out);
  and and_11 (and_11_out, not_14_out, not_15_out);
  and and_12 (and_12_out, S1, not_16_out);
  and and_13 (and_13_out, S1, not_17_out);
  and and_14 (and_14_out, not_18_out, S2);
  and and_15 (and_15_out, S1, not_19_out);
  and and_16 (and_16_out, S1, not_20_out);
  or or_2 (a, and_1_out, S2, and_2_out);
  or or_3 (b, not_21_out, and_3_out, and_4_out);
  or or_4 (d, and_5_out, and_6_out, and_7_out, and_8_out);
  or or_5 (e, and_9_out, and_10_out);
  or or_6 (f, and_11_out, and_12_out, and_13_out);
  or or_7 (g, and_14_out, and_15_out, and_16_out);
endmodule

module Soma_Completa (
  input  Cin,
  input  A,
  input  B,
  output S,
  output Cout
);

  wire and_1_out, and_2_out, xor_1_out;

  xor xor_1 (xor_1_out, A, B);
  and and_1 (and_1_out, A, B);
  xor xor_2 (S, Cin, xor_1_out);
  and and_2 (and_2_out, xor_1_out, Cin);
  or or_1 (Cout, and_2_out, and_1_out);
endmodule

module Multi_2_1 (
  input  in_1,
  input  A,
  input  B,
  output S
);

  wire and_1_out, and_2_out;

  and and_1 (and_1_out, A, ~in_1);  // AND_Gate
  and and_2 (and_2_out, B, in_1);
  or or_1 (S, and_1_out, and_2_out);
endmodule

module Mult_4_1 (
  input  Op1,
  input  Op2,
  input  A,
  input  B,
  input  C,
  input  D,
  output out_7
);

  wire multi_2_1_1_s, multi_2_1_2_s;

  Multi_2_1 multi_2_1_1 (.A(A), .B(B), .S(multi_2_1_1_s), .in_1(Op1));
  Multi_2_1 multi_2_1_2 (.A(C), .B(D), .S(multi_2_1_2_s), .in_1(Op1));
  Multi_2_1 multi_2_1_3 (.A(multi_2_1_1_s), .B(multi_2_1_2_s), .S(out_7), .in_1(Op2));
endmodule
