// Logisim project Registradores.circ as structural Verilog
module FF_4_bits (
  input  D1,
  input  D2,
  input  D3,
  input  D4,
  output out_5,
  output out_6,
  output out_7,
  output out_8
);

  wire clock_1_out, hex_dec_1_a_2, hex_dec_1_b_2, hex_dec_1_c_2, hex_dec_1_d_2, hex_dec_1_e, hex_dec_1_f,
       hex_dec_1_g;

  Clock clock_1 (.out(clock_1_out));
  D_Flip_Flop d_ff_1 (.clk(clock_1_out), .D(D1), .Q(out_5));  // open: Qn, preset, en, reset
  D_Flip_Flop d_ff_2 (.clk(clock_1_out), .D(D2), .Q(out_6));  // open: Qn, preset, en, reset
  D_Flip_Flop d_ff_3 (.clk(clock_1_out), .D(D3), .Q(out_7));  // open: Qn, preset, en, reset
  D_Flip_Flop d_ff_4 (.clk(clock_1_out), .D(D4), .Q(out_8));  // open: Qn, preset, en, reset
  HEX_DEC hex_dec_1 (
    .A(out_5), .B(out_6), .C(out_7), .D(out_8), .a_2(hex_dec_1_a_2), .b_2(hex_dec_1_b_2),
    .c_2(hex_dec_1_c_2), .d_2(hex_dec_1_d_2), .e(hex_dec_1_e), .f(hex_dec_1_f), .g(hex_dec_1_g));
  _7_Segment_Display u_7_segment_display_1 (
    .g(hex_dec_1_g), .f(hex_dec_1_f), .a(hex_dec_1_a_2), .b(hex_dec_1_b_2), .e(hex_dec_1_e),
    .d(hex_dec_1_d_2), .c(hex_dec_1_c_2));  // open: dp
endmodule

module HEX_DEC (
  input  A,
  input  B,
  input  C,
  input  D,
  output a_2,
  output b_2,
  output c_2,
  output d_2,
  output e,
  output f,
  output g
);

  wire and_1_out, and_2_out, and_3_out, and_4_out, and_5_out, and_6_out, and_7_out, and_8_out, and_9_out,
       and_10_out, and_11_out, and_12_out, and_13_out, and_14_out, and_15_out, and_16_out, and_17_out,
       and_18_out, and_19_out, and_20_out, and_21_out, and_22_out, and_23_out, and_24_out, and_25_out,
       and_26_out, and_27_out, and_28_out, and_29_out, and_30_out, and_31_out, and_32_out, and_33_out,
       and_34_out, and_35_out, not_1_out, not_2_out, not_3_out, not_4_out, not_5_out, not_6_out, not_7_out,
       not_8_out, not_9_out, not_10_out, not_11_out, not_12_out, not_13_out, not_14_out, not_15_out,
       not_16_out, not_17_out, not_18_out, not_19_out, not_20_out, not_21_out, not_22_out, not_23_out,
       not_24_out, not_25_out, not_26_out, not_27_out, not_28_out, not_29_out, not_30_out, not_31_out,
       not_32_out, not_33_out, not_34_out, not_35_out, not_36_out, not_37_out, not_38_out, not_39_out,
       not_40_out, not_41_out, not_42_out, not_43_out, not_44_out;

  not not_1 (not_1_out, B);
  and and_1 (and_1_out, not_1_out, not_2_out);
  not not_2 (not_2_out, D);
  not not_3 (not_3_out, A);
  and and_2 (and_2_out, not_3_out, C);
  not not_4 (not_4_out, A);
  and and_3 (and_3_out, not_4_out, B, D);
  and and_4 (and_4_out, B, C);
  not not_5 (not_5_out, B);
  and and_5 (and_5_out, A, not_5_out, not_6_out);
  not not_6 (not_6_out, C);
  and and_6 (and_6_out, A, not_7_out);
  not not_7 (not_7_out, D);
  not not_8 (not_8_out, A);
  and and_7 (and_7_out, not_8_out, not_9_out);
  not not_9 (not_9_out, B);
  not not_10 (not_10_out, A);
  and and_8 (and_8_out, not_10_out, not_11_out, not_12_out);
  not not_11 (not_11_out, C);
  not not_12 (not_12_out, D);
  not not_13 (not_13_out, B);
  and and_9 (and_9_out, not_13_out, not_14_out);
  not not_14 (not_14_out, D);
  not not_15 (not_15_out, A);
  and and_10 (and_10_out, not_15_out, C, D);
  not not_16 (not_16_out, C);
  and and_11 (and_11_out, A, not_16_out, D);
  not not_17 (not_17_out, A);
  and and_12 (and_12_out, not_17_out, not_18_out);
  not not_18 (not_18_out, C);
  not not_19 (not_19_out, A);
  and and_13 (and_13_out, not_19_out, D);
  not not_20 (not_20_out, C);
  and and_14 (and_14_out, not_20_out, D);
  not not_21 (not_21_out, A);
  and and_15 (and_15_out, not_21_out, B);
  and and_16 (and_16_out, A, not_22_out);
  not not_22 (not_22_out, B);
  not not_23 (not_23_out, A);
  not not_24 (not_24_out, B);
  and and_17 (and_17_out, not_23_out, not_24_out, not_25_out);
  not not_25 (not_25_out, D);
  not not_26 (not_26_out, B);
  and and_18 (and_18_out, not_26_out, C, D);
  not not_27 (not_27_out, C);
  and and_19 (and_19_out, B, not_27_out, D);
  and and_20 (and_20_out, B, C, not_28_out);
  not not_28 (not_28_out, D);
  and and_21 (and_21_out, A, not_29_out, not_30_out);
  not not_29 (not_29_out, C);
  not not_30 (not_30_out, D);
  not not_31 (not_31_out, B);
  and and_22 (and_22_out, not_31_out, not_32_out);
  not not_32 (not_32_out, D);
  and and_23 (and_23_out, C, not_33_out);
  not not_33 (not_33_out, D);
  and and_24 (and_24_out, A, C);
  and and_25 (and_25_out, A, B);
  not not_34 (not_34_out, C);
  and and_26 (and_26_out, not_34_out, not_35_out);
  not not_35 (not_35_out, D);
  not not_36 (not_36_out, A);
  and and_27 (and_27_out, not_36_out, B, not_37_out);
  not not_37 (not_37_out, C);
  and and_28 (and_28_out, B, not_38_out);
  not not_38 (not_38_out, D);
  and and_29 (and_29_out, A, not_39_out);
  not not_39 (not_39_out, B);
  and and_30 (and_30_out, A, C);
  not not_40 (not_40_out, B);
  and and_31 (and_31_out, not_40_out, C);
  and and_32 (and_32_out, C, not_41_out);
  not not_41 (not_41_out, D);
  not not_42 (not_42_out, A);
  and and_33 (and_33_out, not_42_out, B, not_43_out);
  not not_43 (not_43_out, C);
  and and_34 (and_34_out, A, not_44_out);
  not not_44 (not_44_out, B);
  and and_35 (and_35_out, A, D);
  or or_1 (b_2, and_7_out, and_8_out, and_9_out, and_10_out, and_11_out);
  or or_2 (c_2, and_12_out, and_13_out, and_14_out, and_15_out, and_16_out);
  or or_3 (d_2, and_17_out, and_18_out, and_19_out, and_20_out, and_21_out);
  or or_4 (e, and_22_out, and_23_out, and_24_out, and_25_out);
  or or_5 (f, and_26_out, and_27_out, and_28_out, and_29_out, and_30_out);
  or or_6 (g, and_31_out, and_32_out, and_33_out, and_34_out, and_35_out);
  or or_7 (a_2, and_1_out, and_2_out, and_3_out, and_4_out, and_5_out, and_6_out);
endmodule

module Rippler_Couter (
  output out_1,
  output out_2,
  output out_3,
  output out_4
);

  wire clock_1_out, d_ff_1_qn, d_ff_2_qn, d_ff_3_qn, d_ff_4_qn, hex_dec_1_a_2, hex_dec_1_b_2, hex_dec_1_c_2,
       hex_dec_1_d_2, hex_dec_1_e, hex_dec_1_f, hex_dec_1_g;

  Clock clock_1 (.out(clock_1_out));
  D_Flip_Flop d_ff_1 (.clk(clock_1_out), .D(d_ff_1_qn), .Q(out_4), .Qn(d_ff_1_qn));  // open: preset, en, reset
  D_Flip_Flop d_ff_2 (.clk(d_ff_1_qn), .D(d_ff_2_qn), .Q(out_3), .Qn(d_ff_2_qn));  // open: preset, en, reset
  D_Flip_Flop d_ff_3 (.clk(d_ff_2_qn), .D(d_ff_3_qn), .Q(out_2), .Qn(d_ff_3_qn));  // open: preset, en, reset
  D_Flip_Flop d_ff_4 (.clk(d_ff_3_qn), .D(d_ff_4_qn), .Q(out_1), .Qn(d_ff_4_qn));  // open: preset, en, reset
  HEX_DEC hex_dec_1 (
    .A(out_1), .B(out_2), .C(out_3), .D(out_4), .a_2(hex_dec_1_a_2), .b_2(hex_dec_1_b_2),
    .c_2(hex_dec_1_c_2), .d_2(hex_dec_1_d_2), .e(hex_dec_1_e), .f(hex_dec_1_f), .g(hex_dec_1_g));
  _7_Segment_Display u_7_segment_display_1 (
    .g(hex_dec_1_g), .f(hex_dec_1_f), .a(hex_dec_1_a_2), .b(hex_dec_1_b_2), .e(hex_dec_1_e),
    .d(hex_dec_1_d_2), .c(hex_dec_1_c_2));  // open: dp
endmodule

module Registrador (
  input  [3:0] BCD,
  input  CLR
);

  wire CLK_out;
  wire [3:0] register_1_q, register_2_q, register_3_q, register_4_q;

  Clock CLK (.out(CLK_out));
  Hex_Digit_Display hex_digit_display_1 (.value(register_1_q));  // open: dp
  Hex_Digit_Display hex_digit_display_2 (.value(register_2_q));  // open: dp
  Register #(.width(4)) register_1 (.D(register_2_q), .Q(register_1_q), .clk(CLK_out), .clr(CLR));  // open: en
  Hex_Digit_Display hex_digit_display_3 (.value(register_4_q));  // open: dp
  Register #(.width(4)) register_2 (.D(register_4_q), .Q(register_2_q), .clk(CLK_out), .clr(CLR));  // open: en
  Hex_Digit_Display hex_digit_display_4 (.value(register_3_q));  // open: dp
  Register #(.width(4)) register_3 (.D(BCD), .Q(register_3_q), .clk(CLK_out), .clr(CLR));  // open: en
  Register #(.width(4)) register_4 (.D(register_3_q), .Q(register_4_q), .clk(CLK_out), .clr(CLR));  // open: en
endmodule

module Bit_register (
  input  in_1,
  input  in_2,
  input  in_3,
  input  in_4,
  input  CLK,
  input  CLR,
  output out_7,
  output out_8,
  output out_9,
  output out_10
);

  wire hex_dec_1_a_2, hex_dec_1_b_2, hex_dec_1_c_2, hex_dec_1_d_2, hex_dec_1_e, hex_dec_1_f, hex_dec_1_g;

  D_Flip_Flop d_ff_1 (.clk(CLK), .D(in_1), .Q(out_7));  // open: Qn, preset, en, reset
  D_Flip_Flop d_ff_2 (.clk(CLK), .D(in_2), .Q(out_8));  // open: Qn, preset, en, reset
  D_Flip_Flop d_ff_3 (.clk(CLK), .D(in_3), .Q(out_9));  // open: Qn, preset, en, reset
  D_Flip_Flop d_ff_4 (.clk(CLK), .D(in_4), .Q(out_10), .reset(CLR));  // open: Qn, preset, en
  HEX_DEC hex_dec_1 (
    .A(out_7), .B(out_8), .C(out_9), .D(out_10), .a_2(hex_dec_1_a_2), .b_2(hex_dec_1_b_2),
    .c_2(hex_dec_1_c_2), .d_2(hex_dec_1_d_2), .e(hex_dec_1_e), .f(hex_dec_1_f), .g(hex_dec_1_g));
  _7_Segment_Display u_7_segment_display_1 (
    .g(hex_dec_1_g), .f(hex_dec_1_f), .a(hex_dec_1_a_2), .b(hex_dec_1_b_2), .e(hex_dec_1_e),
    .d(hex_dec_1_d_2), .c(hex_dec_1_c_2));  // open: dp
endmodule
