// Logisim project Ulas.circ as structural Verilog
module uLA_1Bit (
  input  [1:0] Op1,
  input  Bneg,
  input  Cin,
  input  A,
  input  B,
  output S,
  output Cout
);

  wire and_1_out, multi_2_1_1_s, not_1_out, or_1_out, soma_completa_1_s;

  not not_1 (not_1_out, B);
  Multi_2_1 multi_2_1_1 (.A(B), .B(not_1_out), .S(multi_2_1_1_s), .in_1(Bneg));
  and and_1 (and_1_out, A, B);
  or or_1 (or_1_out, A, B);
  Soma_Completa soma_completa_1 (.Cin(Cin), .A(A), .B(multi_2_1_1_s), .S(soma_completa_1_s), .Cout(Cout));
  _4_1_2 u_4_1_2_1 (.A(and_1_out), .B(or_1_out), .C(soma_completa_1_s), .out_6(S), .Op1(Op1));  // open: D

  // Notes on the sheet:
  //   00 = AND
  //   01 = OR
  //   10 = SUM
endmodule

module ULA_3Bit (
  input  BNeg,
  input  [1:0] Op,
  input  [2:0] A,
  input  [2:0] B,
  output [2:0] out_5,
  output out_6
);

  wire ula_1bit_1_cout, ula_1bit_2_cout;

  uLA_1Bit ula_1bit_1 (.A(A[0]), .B(B[0]), .S(out_5[0]), .Bneg(BNeg), .Cin(BNeg), .Op1(Op), .Cout(ula_1bit_1_cout));
  uLA_1Bit ula_1bit_2 (
    .A(A[1]), .B(B[1]), .S(out_5[1]), .Bneg(BNeg), .Cin(ula_1bit_1_cout), .Op1(Op), .Cout(ula_1bit_2_cout));
  uLA_1Bit ula_1bit_3 (.A(A[2]), .B(B[2]), .S(out_5[2]), .Bneg(BNeg), .Cin(ula_1bit_2_cout), .Op1(Op), .Cout(out_6));
endmodule

module ULA_4Bits (
  input  BNeg,
  input  [1:0] Op,
  input  [3:0] A,
  input  [3:0] B,
  output [3:0] out_5,
  output out_6
);

  wire ula_1bit_1_cout, ula_1bit_2_cout, ula_1bit_3_cout;

  uLA_1Bit ula_1bit_1 (.A(A[0]), .B(B[0]), .S(out_5[0]), .Bneg(BNeg), .Cin(BNeg), .Op1(Op), .Cout(ula_1bit_1_cout));
  uLA_1Bit ula_1bit_2 (
    .A(A[1]), .B(B[1]), .S(out_5[1]), .Bneg(BNeg), .Cin(ula_1bit_1_cout), .Op1(Op), .Cout(ula_1bit_2_cout));
  uLA_1Bit ula_1bit_3 (
    .A(A[2]), .B(B[2]), .S(out_5[2]), .Bneg(BNeg), .Cin(ula_1bit_2_cout), .Op1(Op), .Cout(ula_1bit_3_cout));
  uLA_1Bit ula_1bit_4 (.A(A[3]), .B(B[3]), .S(out_5[3]), .Bneg(BNeg), .Cin(ula_1bit_3_cout), .Op1(Op), .Cout(out_6));

  // Notes on the sheet:
  //   00 = E
  //   01 = OU
  //   10 = SOMA
  //   10+BNeg = SUB
endmodule

module _4_1_2 (
  input  [1:0] Op1,
  input  A,
  input  B,
  input  C,
  input  D,
  output out_6
);

  wire multi_2_1_1_s, multi_2_1_2_s;

  Multi_2_1 multi_2_1_1 (.A(A), .B(B), .S(multi_2_1_1_s), .in_1(Op1[0]));
  Multi_2_1 multi_2_1_2 (.A(C), .B(D), .S(multi_2_1_2_s), .in_1(Op1[0]));
  Multi_2_1 multi_2_1_3 (.A(multi_2_1_1_s), .B(multi_2_1_2_s), .S(out_6), .in_1(Op1[1]));
endmodule

module Hexa_bi (
  input  _0,
  input  _1,
  input  _2,
  input  _3,
  input  _4,
  input  _5,
  input  _6,
  input  _7,
  input  _8,
  input  _9,
  input  A,
  input  B,
  input  C,
  input  D,
  input  E,
  input  F,
  output [3:0] out_17
);

  wire or_1_out, or_2_out, or_3_out, or_4_out, or_5_out, or_6_out, or_7_out, or_8_out;

  or or_1 (or_1_out, _8, _9, A, B);
  or or_2 (or_2_out, C, D, E, F);
  or or_3 (or_3_out, _4, _5, _6, D);
  or or_4 (or_4_out, _7, C, E, F);
  or or_5 (or_5_out, _2, _3, _6, _7);
  or or_6 (or_6_out, A, B, E, F);
  or or_7 (or_7_out, _1, _3, _5, _7);
  or or_8 (or_8_out, _9, B, D, F);
  or or_9 (out_17[3], or_1_out, or_2_out);
  or or_10 (out_17[2], or_3_out, or_4_out);
  or or_11 (out_17[1], or_5_out, or_6_out);
  or or_12 (out_17[0], or_7_out, or_8_out);
endmodule

module Transmissor (
  input  A1,
  input  A2,
  input  A3,
  input  A4,
  input  EN,
  output S0,
  output S1,
  output S2,
  output S3
);

  wire not_1_out, not_2_out, not_3_out, transmission_1_p2;

  // Transmission_Gate transmission_1: pin names not known; wires that end beside it: A4, transmission_1_p2, EN, S3
  not not_1 (not_1_out, EN);
  // Transmission_Gate transmission_2: pin names not known; wires that end beside it: A1, not_1_out, EN, S0
  not not_2 (not_2_out, EN);
  // Transmission_Gate transmission_3: pin names not known; wires that end beside it: A2, not_2_out, EN, S1
  not not_3 (not_3_out, EN);
  // Transmission_Gate transmission_4: pin names not known; wires that end beside it: A3, not_3_out, EN, S2
  not not_4 (transmission_1_p2, EN);

  // Notes on the sheet:
  //   Se você colocar um registrador ligado com o EN,
  //   você conseegue salvar números e digitos e só mudar quando
  //   ativar o EN
endmodule

module _5_BIT_Registrador (
  input  CLK,
  input  PRESET,
  input  EN,
  input  RESET,
  input  A4,
  input  A3,
  input  A2,
  input  A1,
  input  A0,
  output S4,
  output S3,
  output S2,
  output S1,
  output S0
);

  D_Flip_Flop d_ff_1 (.clk(CLK), .D(A4), .Q(S4), .preset(PRESET), .en(EN), .reset(RESET));  // open: Qn
  D_Flip_Flop d_ff_2 (.clk(CLK), .D(A3), .Q(S3), .preset(PRESET), .en(EN), .reset(RESET));  // open: Qn
  D_Flip_Flop d_ff_3 (.clk(CLK), .D(A2), .Q(S2), .preset(PRESET), .en(EN), .reset(RESET));  // open: Qn
  D_Flip_Flop d_ff_4 (.clk(CLK), .D(A1), .Q(S1), .preset(PRESET), .en(EN), .reset(RESET));  // open: Qn
  D_Flip_Flop d_ff_5 (.clk(CLK), .D(A0), .Q(S0), .preset(PRESET), .en(EN), .reset(RESET));  // open: Qn
endmodule

module ULA___logica (
  input  EN,
  input  A3,
  input  A2,
  input  A1,
  input  A0,
  input  B3,
  input  B2,
  input  B1,
  input  B0,
  input  EN_2,
  input  EN_3,
  input  EN_4,
  input  EN_5,
  input  EN_6,
  output S0,
  output S1,
  output S2,
  output S3
);

  wire and_1_out, and_2_out, and_3_out, and_4_out, nand_1_out, nand_2_out, nand_3_out, nand_4_out, nor_1_out,
       nor_2_out, nor_3_out, nor_4_out, or_1_out, or_2_out, or_3_out, or_4_out, xnor_1_out, xnor_2_out,
       xnor_3_out, xnor_4_out, xor_1_out, xor_2_out, xor_3_out, xor_4_out;

  Transmissor transmissor_1 (
    .A1(nor_4_out), .A2(nor_3_out), .A3(nor_2_out), .A4(nor_1_out), .EN(EN), .S0(S0), .S1(S1), .S2(S2),
    .S3(S3));
  Transmissor transmissor_2 (
    .A1(xor_4_out), .A2(xor_3_out), .A3(xor_2_out), .A4(xor_1_out), .EN(EN_2), .S0(S0), .S1(S1), .S2(S2),
    .S3(S3));
  Transmissor transmissor_3 (
    .A1(xnor_4_out), .A2(xnor_3_out), .A3(xnor_2_out), .A4(xnor_1_out), .EN(EN_4), .S0(S0), .S1(S1), .S2(S2),
    .S3(S3));
  nor nor_1 (nor_1_out, A3, B3);
  nor nor_2 (nor_2_out, A2, B2);
  nor nor_3 (nor_3_out, A1, B1);
  nor nor_4 (nor_4_out, A0, B0);
  xor xor_1 (xor_1_out, A3, B3);
  xor xor_2 (xor_2_out, A2, B2);
  xor xor_3 (xor_3_out, A1, B1);
  xor xor_4 (xor_4_out, A0, B0);
  xnor xnor_1 (xnor_1_out, A3, B3);
  xnor xnor_2 (xnor_2_out, A2, B2);
  xnor xnor_3 (xnor_3_out, A1, B1);
  xnor xnor_4 (xnor_4_out, A0, B0);
  and and_1 (and_1_out, A0, B0);
  and and_2 (and_2_out, A1, B1);
  and and_3 (and_3_out, A2, B2);
  and and_4 (and_4_out, A3, B3);
  or or_1 (or_1_out, A0, B0);
  or or_2 (or_2_out, A1, B1);
  or or_3 (or_3_out, A2, B2);
  or or_4 (or_4_out, A3, B3);
  nand nand_1 (nand_1_out, B0, A0);
  nand nand_2 (nand_2_out, B1, A1);
  nand nand_3 (nand_3_out, B2, A2);
  nand nand_4 (nand_4_out, B3, A3);
  Transmissor transmissor_4 (
    .A1(and_1_out), .A2(and_2_out), .A3(and_3_out), .A4(and_4_out), .EN(EN_3), .S0(S0), .S1(S1), .S2(S2),
    .S3(S3));
  Transmissor transmissor_5 (
    .A1(or_1_out), .A2(or_2_out), .A3(or_3_out), .A4(or_4_out), .EN(EN_5), .S0(S0), .S1(S1), .S2(S2), .S3(S3));
  Transmissor transmissor_6 (
    .A1(nand_1_out), .A2(nand_2_out), .A3(nand_3_out), .A4(nand_4_out), .EN(EN_6), .S0(S0), .S1(S1), .S2(S2),
    .S3(S3));
endmodule

module Calc_Hex (
  input  BNeg,
  input  _0,
  input  _1,
  input  _2,
  input  _3,
  input  _4,
  input  _5,
  input  _6,
  input  _7,
  input  _8,
  input  _9,
  input  A,
  input  B,
  input  C,
  input  D,
  input  E,
  input  F,
  input  pos,
  input  _0_2,
  input  _1_2,
  input  _2_2,
  input  _3_2,
  input  _4_2,
  input  _5_2,
  input  _6_2,
  input  _7_2,
  input  _8_2,
  input  _9_2,
  input  A_2,
  input  B_2,
  input  C_2,
  input  D_2,
  input  E_2,
  input  F_2
);

  wire and_1_out, hex_7seg_1_a, hex_7seg_1_b, hex_7seg_1_c, hex_7seg_1_d, hex_7seg_1_e, hex_7seg_1_f,
       hex_7seg_1_g, not_1_out, ula_4bits_1_out_6;
  wire [3:0] comple_2_1_out_2, eq_1_s0, hexa_bi_1_out_17, hexa_bi_2_out_17, ula_4bits_1_out_5;

  Hexa_bi hexa_bi_1 (
    ._0(_0), ._1(_1), ._2(_2), ._3(_3), ._4(_4), ._5(_5), ._6(_6), ._7(_7), ._8(_8), ._9(_9), .A(A), .B(B),
    .C(C), .D(D), .E(E), .F(F), .out_17(hexa_bi_1_out_17));
  Hexa_bi hexa_bi_2 (
    ._0(_0_2), ._1(_1_2), ._2(_2_2), ._3(_3_2), ._4(_4_2), ._5(_5_2), ._6(_6_2), ._7(_7_2), ._8(_8_2),
    ._9(_9_2), .A(A_2), .B(B_2), .C(C_2), .D(D_2), .E(E_2), .F(F_2), .out_17(hexa_bi_2_out_17));
  ULA_4Bits ula_4bits_1 (
    .A(hexa_bi_1_out_17), .B(hexa_bi_2_out_17), .out_5(ula_4bits_1_out_5), .out_6(ula_4bits_1_out_6),
    .BNeg(BNeg), .Op(2'b10));
  not not_1 (not_1_out, pos);
  Eq eq_1 (.A1(ula_4bits_1_out_5), .EN(pos), .S0(eq_1_s0));
  Comple_2 comple_2_1 (.in_1(ula_4bits_1_out_5), .out_2(comple_2_1_out_2));
  Eq eq_2 (.A1(comple_2_1_out_2), .EN(not_1_out), .S0(eq_1_s0));
  and and_1 (and_1_out, ula_4bits_1_out_6, ~BNeg);  // AND_Gate
  Hex_7seg hex_7seg_1 (
    .a0(eq_1_s0[3]), .a1(eq_1_s0[2]), .a2(eq_1_s0[1]), .a3(eq_1_s0[0]), .A(hex_7seg_1_a), .B(hex_7seg_1_b),
    .C(hex_7seg_1_c), .D(hex_7seg_1_d), .E(hex_7seg_1_e), .F(hex_7seg_1_f), .G(hex_7seg_1_g));
  _7_Segment_Display u_7_segment_display_1 (.b(and_1_out), .c(and_1_out));  // open: g, f, a, e, d, dp
  _7_Segment_Display u_7_segment_display_2 (
    .g(hex_7seg_1_g), .f(hex_7seg_1_f), .a(hex_7seg_1_a), .b(hex_7seg_1_b), .e(hex_7seg_1_e),
    .d(hex_7seg_1_d), .c(hex_7seg_1_c));  // open: dp
endmodule

module Hex_7seg (
  input  a0,
  input  a1,
  input  a2,
  input  a3,
  output A,
  output B,
  output C,
  output D,
  output E,
  output F,
  output G
);

  wire and_1_out, and_2_out, and_3_out, and_4_out, and_5_out, and_6_out, and_7_out, and_8_out, and_9_out,
       and_10_out, and_11_out, and_12_out, and_13_out, and_14_out, and_15_out, and_16_out, and_17_out,
       and_18_out, and_19_out, and_20_out, and_21_out, and_22_out, and_23_out, and_24_out, and_25_out,
       and_26_out, and_27_out, and_28_out, and_29_out, and_30_out, and_31_out, and_32_out, and_33_out,
       not_1_out, not_2_out, not_3_out, not_4_out, not_5_out, not_6_out, not_7_out, not_8_out, not_9_out,
       not_10_out, not_11_out, not_12_out, not_13_out, not_14_out, not_15_out, not_16_out, not_17_out,
       not_18_out, not_19_out, not_20_out, not_21_out, not_22_out, not_23_out, not_24_out, not_25_out,
       not_26_out, not_27_out, not_28_out, not_29_out, not_30_out, not_31_out, not_32_out, not_33_out,
       not_34_out, not_35_out, not_36_out, not_37_out, not_38_out, not_39_out, not_40_out, not_41_out,
       not_42_out, not_43_out, not_44_out, not_45_out, not_46_out;

  not not_1 (not_1_out, a0);
  and and_1 (and_1_out, not_1_out, not_2_out, not_3_out);
  not not_2 (not_2_out, a1);
  not not_3 (not_3_out, a3);
  not not_4 (not_4_out, a0);
  and and_2 (and_2_out, not_4_out, a2);
  not not_5 (not_5_out, a0);
  and and_3 (and_3_out, not_5_out, a1, a3);
  and and_4 (and_4_out, a1, a2);
  not not_6 (not_6_out, a1);
  and and_5 (and_5_out, a0, not_6_out, not_7_out);
  not not_7 (not_7_out, a2);
  and and_6 (and_6_out, a0, not_8_out, not_9_out);
  not not_8 (not_8_out, a2);
  not not_9 (not_9_out, a3);
  not not_10 (not_10_out, a3);
  not not_11 (not_11_out, a0);
  and and_7 (and_7_out, not_11_out, not_12_out);
  not not_12 (not_12_out, a1);
  not not_13 (not_13_out, a0);
  and and_8 (and_8_out, not_13_out, not_14_out, not_15_out);
  not not_14 (not_14_out, a2);
  not not_15 (not_15_out, a3);
  not not_16 (not_16_out, a1);
  and and_9 (and_9_out, not_16_out, not_17_out);
  not not_17 (not_17_out, a3);
  and and_10 (and_10_out, a1, a2, a3);
  not not_18 (not_18_out, a2);
  and and_11 (and_11_out, a0, not_18_out, a3);
  not not_19 (not_19_out, a0);
  and and_12 (and_12_out, not_19_out, not_20_out);
  not not_20 (not_20_out, a2);
  not not_21 (not_21_out, a0);
  and and_13 (and_13_out, not_21_out, a1);
  and and_14 (and_14_out, a0, not_22_out);
  not not_22 (not_22_out, a1);
  not not_23 (not_23_out, a0);
  and and_15 (and_15_out, not_23_out, not_24_out, not_25_out);
  not not_24 (not_24_out, a1);
  not not_25 (not_25_out, a3);
  not not_26 (not_26_out, a1);
  and and_16 (and_16_out, not_26_out, a2, a3);
  and and_17 (and_17_out, a1, not_27_out, a3);
  not not_27 (not_27_out, a2);
  and and_18 (and_18_out, a1, a2, not_28_out);
  not not_28 (not_28_out, a3);
  not not_29 (not_29_out, a2);
  and and_19 (and_19_out, a0, not_29_out, not_30_out);
  not not_30 (not_30_out, a3);
  not not_31 (not_31_out, a1);
  and and_20 (and_20_out, not_31_out, not_32_out);
  not not_32 (not_32_out, a3);
  and and_21 (and_21_out, a2, not_33_out);
  not not_33 (not_33_out, a3);
  not not_34 (not_34_out, a1);
  and and_22 (and_22_out, a0, not_34_out, a2);
  and and_23 (and_23_out, a0, a1, not_35_out);
  not not_35 (not_35_out, a2);
  not not_36 (not_36_out, a2);
  and and_24 (and_24_out, not_36_out, not_37_out);
  not not_37 (not_37_out, a3);
  not not_38 (not_38_out, a0);
  and and_25 (and_25_out, not_38_out, a1, not_39_out);
  not not_39 (not_39_out, a2);
  and and_26 (and_26_out, a1, not_40_out);
  not not_40 (not_40_out, a3);
  and and_27 (and_27_out, a0, not_41_out);
  not not_41 (not_41_out, a1);
  not not_42 (not_42_out, a1);
  and and_28 (and_28_out, not_42_out, a2);
  and and_29 (and_29_out, a2, not_43_out);
  not not_43 (not_43_out, a3);
  not not_44 (not_44_out, a0);
  and and_30 (and_30_out, not_44_out, a1, not_45_out);
  not not_45 (not_45_out, a2);
  and and_31 (and_31_out, a0, not_46_out);
  not not_46 (not_46_out, a1);
  and and_32 (and_32_out, a0, a3);
  and and_33 (and_33_out, a0, a2, not_10_out);
  or or_1 (B, and_7_out, and_8_out, and_9_out, and_10_out, and_11_out);
  or or_2 (C, and_12_out, a3, and_13_out, and_14_out);
  or or_3 (D, and_15_out, and_16_out, and_17_out, and_18_out, and_19_out);
  or or_4 (E, and_20_out, and_21_out, and_22_out, and_23_out);
  or or_5 (F, and_24_out, and_25_out, and_26_out, and_27_out);
  or or_6 (G, and_28_out, and_29_out, and_30_out, and_31_out, and_32_out);
  or or_7 (A, and_1_out, and_2_out, and_3_out, and_4_out, and_5_out, and_6_out, and_33_out);
endmodule

module Comple_2 (
  input  [3:0] in_1,
  output [3:0] out_2
);

  wire [3:0] equalizador_1_out_3;

  Equalizador equalizador_1 (.A(in_1), .B(4'b1111), .out_3(equalizador_1_out_3));
  ULA_4Bits ula_4bits_1 (.A(equalizador_1_out_3), .B(4'b1111), .out_5(out_2), .BNeg(1'b1), .Op(2'b10));  // open: out_6
endmodule

module Equalizador (
  input  [3:0] A,
  input  [3:0] B,
  output [3:0] out_3
);

  xor xor_1 (out_3[0], A[0], B[0]);
  xor xor_2 (out_3[1], A[1], B[1]);
  xor xor_3 (out_3[2], A[2], B[2]);
  xor xor_4 (out_3[3], A[3], B[3]);
endmodule

module Eq (
  input  [3:0] A1,
  input  EN,
  output [3:0] S0
);

  wire not_1_out, not_2_out, not_3_out, transmission_1_p2;

  // Transmission_Gate transmission_1: pin names not known; wires that end beside it: A1[3], transmission_1_p2, EN, S0[3]
  not not_1 (not_1_out, EN);
  // Transmission_Gate transmission_2: pin names not known; wires that end beside it: A1[0], not_1_out, EN, S0[0]
  not not_2 (not_2_out, EN);
  // Transmission_Gate transmission_3: pin names not known; wires that end beside it: A1[1], not_2_out, EN, S0[1]
  not not_3 (not_3_out, EN);
  // Transmission_Gate transmission_4: pin names not known; wires that end beside it: A1[2], not_3_out, EN, S0[2]
  not not_4 (transmission_1_p2, EN);
endmodule
